# Fritzing sketch single chip3 (saved by Fritzing 0.9.3b)

parts:
  元件1 = Arduino Nano (Rev3.0)
  VCC1 = Battery block 9V
  GY1 = MPU-6050 Board GY-521 [form="♀ (female)" package=THT]
  元件2 = Bluetooth HC-05 Macho
  R1 = Slide Potentiometer [maximum_resistance=10kΩ]
  S1 = Round Pushbutton
  S2 = Momentary Switch [package=ksa_sealed_tac_switch]
  LED1 = RGB LED (com. cathode, rgb) [package="5 mm [THT]"]

nets:
  N1: 元件1.D1/TX, 元件2.RXD
  N2: 元件1.D0/RX, 元件2.TXD
  GND: 元件1.GND, VCC1.-, GY1.pin2, 元件2.GND, R1.leg1, LED1.common_cathode
  N3: 元件1.D2, GY1.pin8
  N4: 元件1.D3, LED1.blue_anode
  N5: 元件1.D4, LED1.green_anode
  N6: 元件1.D5, LED1.red_anode
  N7: 元件1.D7, S2.3
  N8: 元件1.VIN, S1.leg1
  5V: 元件1.5V, GY1.pin1, 元件2.VCC, R1.leg2
  N9: 元件1.A5, GY1.pin3
  N10: 元件1.A4, GY1.pin4
  N11: 元件1.A3, R1.wiper
  N12: VCC1.+, S1.leg0

notes:
  bluetooth
  arduino nano
  accelerometer
  Slide switch
  on/off switch
  switch

custom parts:
  MPU-6050 Board GY-521: Acelerometro y Giroscopio MPU-6050 Board GY-521
